// Logisim project moongrt.circ as structural Verilog: 5 circuits, main circuit main
module main (
  input  in_1,
  input  EN
);

  wire and_1_out, CLK, clock_1_out, comparator_1_lt, comparator_2_lt, comparator_3_gt, id_1_byte, id_1_immen,
       id_1_jump, id_1_memren, id_1_memwen, or_1_out, or_2_out, rgb_video_1_p3;
  wire [3:0] decoder_1_out0, multiplexer_4_out;
  wire [15:0] counter_1_q;
  wire [17:0] ex_1_exout_2;
  wire [23:0] bit_extender_1_out;
  wire [31:0] ex_1_exout, id_1_d1, id_1_d2, id_1_imm, multiplexer_1_out, multiplexer_3_out, pc_1_pc_current,
       pc_1_pc_next, ram_1_dout, rom_1_data;

  Counter #(.max('hffff), .width(16)) counter_1 (.clk(CLK), .Q(counter_1_q));  // open: clr, load, up, count, D, carry
  PC pc_1 (
    .JUMP_ADDR({ex_1_exout[31:20], ex_1_exout_2, ex_1_exout[1:0]}), .JUMP(id_1_jump), .CLK(CLK),
    .PC_Next(pc_1_pc_next), .PC_Current(pc_1_pc_current));
  // Probe on pc_1_pc_current[21:2]
  // Probe on multiplexer_1_out
  Multiplexer #(.width(32)) multiplexer_1 (
    .in0({ex_1_exout[31:20], ex_1_exout_2, ex_1_exout[1:0]}), .in1(pc_1_pc_next), .out(multiplexer_1_out),
    .sel(id_1_jump));
  Multiplexer multiplexer_2 (.in0(in_1), .in1(clock_1_out), .out(CLK), .sel(or_1_out));
  Clock clock_1 (.out(clock_1_out));
  or or_1 (or_1_out, EN, comparator_1_lt);
  Comparator #(.width(16)) comparator_1 (.a(counter_1_q), .b(16'h2000), .lt(comparator_1_lt));  // open: gt, eq
  ROM #(.addrWidth(20), .dataWidth(32)) rom_1 (.addr(pc_1_pc_current[21:2]), .data(rom_1_data));
  ID id_1 (
    .EXdata(multiplexer_1_out), .MEMdata(ram_1_dout), .Bsel(ex_1_exout[1:0]), .CLK(CLK), .Inst(rom_1_data),
    .D1(id_1_d1), .D2(id_1_d2), .IMM(id_1_imm), .IMMen(id_1_immen), .JUMP(id_1_jump), .MEMRen(id_1_memren),
    .MEMWen(id_1_memwen), .Byte(id_1_byte));
  Decoder #(.enable("false"), .select(2)) decoder_1 (
    .out0(decoder_1_out0[0]), .out1(decoder_1_out0[1]), .out2(decoder_1_out0[2]), .out3(decoder_1_out0[3]),
    .sel(ex_1_exout[1:0]));
  // Probe on id_1_d1
  // Probe on id_1_d2
  and and_1 (and_1_out, id_1_memwen, or_2_out);
  Multiplexer #(.width(32)) multiplexer_3 (
    .in0(id_1_d2), .in1({id_1_d2[7:0], id_1_d2[7:0], id_1_d2[7:0], id_1_d2[7:0]}), .out(multiplexer_3_out),
    .sel(id_1_byte));
  RAM #(.addrWidth(18), .asyncread("true"), .byteenables("byteEnables"), .dataWidth(32), .\type ("nonvolatile")) ram_1 (
    .addr(ex_1_exout_2), .we(and_1_out), .oe(id_1_memren), .clk(CLK), .din(multiplexer_3_out),
    .dout(ram_1_dout), .be3(multiplexer_4_out[3]), .be2(multiplexer_4_out[2]), .be1(multiplexer_4_out[1]),
    .be0(multiplexer_4_out[0]));
  Multiplexer #(.width(4)) multiplexer_4 (
    .in0(4'b1111), .in1(decoder_1_out0), .out(multiplexer_4_out), .sel(id_1_byte));
  // Probe on {ex_1_exout[31:20], ex_1_exout_2, ex_1_exout[1:0]}
  EX ex_1 (
    .R1(id_1_d1), .R2(id_1_d2), .IMM(id_1_imm), .IMMen(id_1_immen),
    .EXout({ex_1_exout[31:20], ex_1_exout_2, ex_1_exout[1:0]}));
  // Probe on ram_1_dout
  Comparator #(.width(32)) comparator_2 (
    .a({ex_1_exout[31:20], ex_1_exout_2, ex_1_exout[1:0]}), .b(32'h20000000), .lt(comparator_2_lt));  // open: gt, eq
  Comparator #(.width(32)) comparator_3 (
    .a({ex_1_exout[31:20], ex_1_exout_2, ex_1_exout[1:0]}), .b(32'h20040000), .gt(comparator_3_gt));  // open: eq, lt
  // Probe on ex_1_exout_2[7:0]
  // Probe on ex_1_exout_2[15:8]
  Bit_Extender #(.in_width(32), .out_width(24), .\type ("one")) bit_extender_1 (.in(id_1_d2), .out(bit_extender_1_out));
  or or_2 (or_2_out, comparator_2_lt, comparator_3_gt);
  // RGB_Video #(.height(256), .width(256)) rgb_video_1: pin names not known; wires that end beside it: 1'b0, CLK, rgb_video_1_p3, ex_1_exout_2[7:0], ex_1_exout_2[15:8], bit_extender_1_out
  not not_1 (rgb_video_1_p3, or_2_out);
  // Probe on bit_extender_1_out

  // Notes on the sheet:
  //   EN: initial=0x1
  //   contents of rom_1 (hex, n*v repeats v):
  //   413 93137 10113 10b7 dbc08093 80e7 fe012823 fea10923 fea12423 fe914203 fe4109a3 ff012783 f787b3
  //   f787b3 4b6b7 af868693 fdc10113 d787b3 10000713 f12423 10593 100793 b00513 2112023 12023 12223 e12623
  //   e12823 f10a23 10b7 a8408093 80e7 2012083 2410113 8067 ff410113 112423 10b7 a7c08093 80e7 513 1800093
  //   80e7 812083 513 c10113 8067 852583 feb12823 fe812e23 3437 80840413 ff014183 3401b3 1c183 ff114203
  //   440233 24203 4181b3 ff214203 440233 24203 4181b3 ff314203 440233 24203 4181b3 3237 80020213 320233
  //   24203 ffc12403 420233 420233 410233 11b7 86418193 fe312823 14800193 fe312623 fec22203 20067 1052703
  //   52683 452783 fe810113 e12423 112a23 812823 912623 fed12823 fef12623 13737 a0070713 fe012223 ff314203
  //   fe4102a3 fef14203 fe410223 fe412203 470233 24203 fe4105a3 ff214203 fe4102a3 fee14203 fe410223
  //   fe412203 470233 24203 fe410523 ff114203 fe4102a3 fed14203 fe410223 fe412203 470233 24203 fe4104a3
  //   ff014203 fe4102a3 fec14203 fe410223 fe412203 470233 24203 fe410423 fe812703 c52603 fee12823 fe812e23
  //   3437 80840413 ff014183 3401b3 1c183 ff114203 440233 24203 4181b3 ff214203 440233 24203 4181b3
  //   ff314203 440233 24203 4181b3 3237 80020213 320233 24203 ffc12403 420233 420233 410233 66800193
  //   fe312823 28800193 fe312623 fec22203 20067 c68733 10000513 fe812e23 fe912c23 fee12823 50413 ff012483
  //   fe812423 feb14183 3181b3 fe312423 fe914183 3181b3 fe912423 feb14203 420233 fe412423 fe914203 4181b3
  //   3181b3 fe312a23 fe912423 33237 90020213 feb14183 4181b3 1c183 fe3103a3 fea14183 4181b3 1c183
  //   fe310323 fe914183 4181b3 1c183 fe3102a3 fe814183 4181b3 1c183 fe310223 ff412183 fe412203 440233
  //   120213 fe412423 feb14203 420233 fe412423 fe914203 4181b3 3237 90820213 320233 ff812483 ffc12403
  //   24203 420233 420233 410233 11b7 86818193 fe312823 39000193 fe312623 fec22203 20067 812703 10000513
  //   e78733 fe812e23 fe912c23 fee12823 50413 ff012483 fe812423 feb14183 3181b3 fe312423 fe914183 3181b3
  //   fe912423 feb14203 420233 fe412423 fe914203 4181b3 3181b3 fe312a23 fe912423 33237 90020213 feb14183
  //   4181b3 1c183 fe3103a3 fea14183 4181b3 1c183 fe310323 fe914183 4181b3 1c183 fe3102a3 fe814183 4181b3
  //   1c183 fe310223 ff412183 fe412203 440233 120213 fe412423 feb14203 420233 fe412423 fe914203 4181b3
  //   3237 90820213 320233 ff812483 ffc12403 24203 420233 420233 410233 11b7 86818193 fe312823 49c00193
  //   fe312623 fec22203 20067 8*f787b3 d787b3 f787b3 f787b3 20000437 f40433 812783 c60633 c60633 fef12423
  //   feb14183 3181b3 fe312423 fe914183 fff78213 fe412423 feb14203 420233 fe412423 fe914203 4181b3 3237
  //   91820213 418233 24203 420233 420233 410233 65400193 fe312823 54000193 fe312623 fec22203 20067 493
  //   40513 b12223 c12023 10b7 de008093 80e7 12603 412583 812783 148493 40040413 c585b3 fef12823 fe912623
  //   fe812e23 fe912c23 2437 70040413 ff014183 340233 100193 320023 fec14183 3401b3 18023 24183 ff114483
  //   940233 100493 920023 fed14483 9404b3 48023 24483 9181b3 ff214483 940233 100493 920023 fee14483
  //   9404b3 48023 24483 9181b3 ff314483 940233 100493 920023 fef14483 9404b3 48023 24483 9181b3 3237
  //   80020213 320233 24203 ff812483 ffc12403 420233 420233 410233 65400193 fe312823 54400193 fe312623
  //   fec22203 20067 1412083 1012403 c12483 1810113 8067 10000713 fec12823 fee12623 fe812e23 fe912c23 2437
  //   70040413 ff014183 340233 100193 320023 fec14183 3401b3 18023 24183 ff114483 940233 100493 920023
  //   fed14483 9404b3 48023 24483 9181b3 ff214483 940233 100493 920023 fee14483 9404b3 48023 24483 9181b3
  //   ff314483 940233 100493 920023 fef14483 9404b3 48023 24483 9181b3 3237 80020213 320233 24203 ff812483
  //   ffc12403 420233 420233 410233 74c00193 fe312823 28800193 fe312623 fec22203 20067 812703 fee12823
  //   fec12623 fe812e23 fe912c23 2437 70040413 ff014183 340233 100193 320023 fec14183 3401b3 18023 24183
  //   ff114483 940233 100493 920023 fed14483 9404b3 48023 24483 9181b3 ff214483 940233 100493 920023
  //   fee14483 9404b3 48023 24483 9181b3 ff314483 940233 100493 920023 fef14483 9404b3 48023 24483 9181b3
  //   3237 80020213 320233 24203 ff812483 ffc12403 420233 420233 410233 11b7 83418193 fe312823 39000193
  //   fe312623 fec22203 20067 1012403 1412083 c12483 40637 20000537 1810113 1237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
endmodule

module PC (
  input  [31:0] JUMP_ADDR,
  input  JUMP,
  input  CLK,
  output [31:0] PC_Next,
  output [31:0] PC_Current
);

  wire [31:0] multiplexer_1_out;

  Multiplexer #(.width(32)) multiplexer_1 (.in0(PC_Next), .in1(JUMP_ADDR), .out(multiplexer_1_out), .sel(JUMP));
  Register #(.width(32)) register_1 (.D(multiplexer_1_out), .en(1'b1), .clk(CLK), .Q(PC_Current));  // open: clr
  Adder #(.width(32)) adder_1 (.a(32'h4), .b(PC_Current), .out(PC_Next));  // open: cin, cout
endmodule

module GPR (
  input  [3:0] Raddr1,
  input  [3:0] Raddr2,
  input  CLK,
  input  [31:0] Wdata,
  input  [3:0] Waddr,
  input  Wen,
  output [31:0] Rdata1,
  output [31:0] Rdata2
);

  wire decoder_1_out1, decoder_1_out2, decoder_1_out3, decoder_1_out4, decoder_1_out5, decoder_1_out6,
       decoder_1_out7, decoder_1_out8, decoder_1_out9, decoder_1_out10, decoder_1_out11, decoder_1_out12,
       decoder_1_out13, decoder_1_out14, decoder_1_out15;
  wire [31:0] register_1_q, register_2_q, register_3_q, register_4_q, register_5_q, register_6_q,
       register_7_q, register_8_q, register_9_q, register_10_q, register_11_q, register_12_q, register_13_q,
       register_14_q, register_15_q, register_16_q;

  Decoder #(.select(4)) decoder_1 (
    .out1(decoder_1_out1), .out2(decoder_1_out2), .out3(decoder_1_out3), .out4(decoder_1_out4),
    .out5(decoder_1_out5), .out6(decoder_1_out6), .out7(decoder_1_out7), .out8(decoder_1_out8),
    .out9(decoder_1_out9), .out10(decoder_1_out10), .out11(decoder_1_out11), .out12(decoder_1_out12),
    .out13(decoder_1_out13), .out14(decoder_1_out14), .out15(decoder_1_out15), .sel(Waddr), .en(Wen));  // open: out0
  Register #(.width(32)) register_1 (.D(Wdata), .en(1'b0), .clk(CLK), .Q(register_1_q));  // open: clr
  Register #(.width(32)) register_2 (.D(Wdata), .en(decoder_1_out8), .clk(CLK), .Q(register_2_q));  // open: clr
  Register #(.width(32)) register_3 (.D(Wdata), .en(decoder_1_out1), .clk(CLK), .Q(register_3_q));  // open: clr
  Register #(.width(32)) register_4 (.D(Wdata), .en(decoder_1_out9), .clk(CLK), .Q(register_4_q));  // open: clr
  Register #(.width(32)) register_5 (.D(Wdata), .en(decoder_1_out2), .clk(CLK), .Q(register_5_q));  // open: clr
  Register #(.width(32)) register_6 (.D(Wdata), .en(decoder_1_out10), .clk(CLK), .Q(register_6_q));  // open: clr
  Register #(.width(32)) register_7 (.D(Wdata), .en(decoder_1_out3), .clk(CLK), .Q(register_7_q));  // open: clr
  Register #(.width(32)) register_8 (.D(Wdata), .en(decoder_1_out11), .clk(CLK), .Q(register_8_q));  // open: clr
  Register #(.width(32)) register_9 (.D(Wdata), .en(decoder_1_out4), .clk(CLK), .Q(register_9_q));  // open: clr
  Register #(.width(32)) register_10 (.D(Wdata), .en(decoder_1_out12), .clk(CLK), .Q(register_10_q));  // open: clr
  Register #(.width(32)) register_11 (.D(Wdata), .en(decoder_1_out5), .clk(CLK), .Q(register_11_q));  // open: clr
  Register #(.width(32)) register_12 (.D(Wdata), .en(decoder_1_out13), .clk(CLK), .Q(register_12_q));  // open: clr
  Register #(.width(32)) register_13 (.D(Wdata), .en(decoder_1_out6), .clk(CLK), .Q(register_13_q));  // open: clr
  Register #(.width(32)) register_14 (.D(Wdata), .en(decoder_1_out14), .clk(CLK), .Q(register_14_q));  // open: clr
  Register #(.width(32)) register_15 (.D(Wdata), .en(decoder_1_out7), .clk(CLK), .Q(register_15_q));  // open: clr
  Register #(.width(32)) register_16 (.D(Wdata), .en(decoder_1_out15), .clk(CLK), .Q(register_16_q));  // open: clr
  Multiplexer #(.select(4), .width(32)) multiplexer_1 (
    .in0(register_1_q), .in1(register_3_q), .in2(register_5_q), .in3(register_7_q), .in4(register_9_q),
    .in5(register_11_q), .in6(register_13_q), .in7(register_15_q), .in8(register_2_q), .in9(register_4_q),
    .in10(register_6_q), .in11(register_8_q), .in12(register_10_q), .in13(register_12_q),
    .in14(register_14_q), .in15(register_16_q), .out(Rdata1), .sel(Raddr1));
  Multiplexer #(.select(4), .width(32)) multiplexer_2 (
    .in0(register_1_q), .in1(register_3_q), .in2(register_5_q), .in3(register_7_q), .in4(register_9_q),
    .in5(register_11_q), .in6(register_13_q), .in7(register_15_q), .in8(register_2_q), .in9(register_4_q),
    .in10(register_6_q), .in11(register_8_q), .in12(register_10_q), .in13(register_12_q),
    .in14(register_14_q), .in15(register_16_q), .out(Rdata2), .sel(Raddr2));
  // Probe on register_1_q
  // Probe on register_3_q
  // Probe on register_5_q
  // Probe on register_7_q
  // Probe on register_9_q
  // Probe on register_11_q
  // Probe on register_13_q
  // Probe on register_15_q
  // Probe on register_2_q
  // Probe on register_4_q
  // Probe on register_6_q
  // Probe on register_8_q
  // Probe on register_10_q
  // Probe on register_12_q
  // Probe on register_14_q
  // Probe on register_16_q
endmodule

module ID (
  input  [31:0] EXdata,
  input  [31:0] MEMdata,
  input  [1:0] Bsel,
  input  CLK,
  input  [31:0] Inst,
  output [31:0] D1,
  output [31:0] D2,
  output [31:0] IMM,
  output IMMen,
  output JUMP,
  output MEMRen,
  output MEMWen,
  output Byte
);

  wire comparator_1_eq, comparator_2_eq, comparator_3_eq, comparator_4_eq, comparator_5_eq, comparator_6_eq,
       comparator_7_eq, not_1_out, or_1_out, or_2_out, priority_encoder_1_en_out;
  wire [1:0] priority_encoder_1_out;
  wire [7:0] multiplexer_1_out;
  wire [31:0] bit_extender_1_out, bit_extender_2_out, bit_extender_3_out, multiplexer_2_out,
       multiplexer_4_out;

  // Probe on {Inst[14:12], Inst[6:0]}
  assign bit_extender_1_out = {{20{Inst[31]}}, Inst[31:20]};  // Bit_Extender bit_extender_1
  // Probe on bit_extender_1_out
  assign bit_extender_2_out = {{20{Inst[31]}}, {Inst[31:25], Inst[11:7]}};  // Bit_Extender bit_extender_2
  Comparator #(.width(10)) comparator_1 (
    .a(10'h33), .b({Inst[14:12], Inst[6:0]}), .eq(comparator_1_eq));  // open: gt, lt
  Comparator #(.width(10)) comparator_2 (
    .a(10'h13), .b({Inst[14:12], Inst[6:0]}), .eq(comparator_2_eq));  // open: gt, lt
  Comparator #(.width(7)) comparator_3 (.a(7'b0110111), .b(Inst[6:0]), .eq(comparator_3_eq));  // open: gt, lt
  Comparator #(.width(10)) comparator_4 (
    .a(10'h103), .b({Inst[14:12], Inst[6:0]}), .eq(comparator_4_eq));  // open: gt, lt
  Comparator #(.width(10)) comparator_5 (
    .a(10'h203), .b({Inst[14:12], Inst[6:0]}), .eq(comparator_5_eq));  // open: gt, lt
  Comparator #(.width(10)) comparator_6 (
    .a(10'h123), .b({Inst[14:12], Inst[6:0]}), .eq(comparator_6_eq));  // open: gt, lt
  Comparator #(.width(10)) comparator_7 (
    .a(10'h23), .b({Inst[14:12], Inst[6:0]}), .eq(comparator_7_eq));  // open: gt, lt
  Comparator #(.width(10)) comparator_8 (.a(10'h67), .b({Inst[14:12], Inst[6:0]}), .eq(JUMP));  // open: gt, lt
  // Probe on bit_extender_2_out
  // Probe on {Inst[31:12], {12{1'b0}}}
  Multiplexer #(.select(2), .width(8)) multiplexer_1 (
    .in0(MEMdata[7:0]), .in1(MEMdata[15:8]), .in2(MEMdata[23:16]), .in3(MEMdata[31:24]),
    .out(multiplexer_1_out), .sel(Bsel));
  or or_1 (or_1_out, comparator_6_eq, comparator_7_eq);
  Multiplexer #(.width(32)) multiplexer_2 (
    .in0(MEMdata), .in1(bit_extender_3_out), .out(multiplexer_2_out), .sel(Byte));
  assign bit_extender_3_out = {{24{1'b0}}, multiplexer_1_out};  // Bit_Extender bit_extender_3
  // Probe on Inst[18:15]
  // Probe on Inst[23:20]
  or or_2 (or_2_out, comparator_2_eq, comparator_4_eq, comparator_5_eq, JUMP);
  Multiplexer #(.select(2), .width(32)) multiplexer_3 (
    .in0(bit_extender_1_out), .in1(bit_extender_2_out), .in2({Inst[31:12], {12{1'b0}}}), .in3({32{1'b0}}),
    .out(IMM), .sel(priority_encoder_1_out));
  Multiplexer #(.width(32)) multiplexer_4 (
    .in0(EXdata), .in1(multiplexer_2_out), .out(multiplexer_4_out), .sel(MEMRen));
  // Probe on Inst[10:7]
  not not_1 (not_1_out, MEMWen);
  // Probe on priority_encoder_1_en_out
  // Probe on priority_encoder_1_out
  Priority_Encoder #(.select(2)) priority_encoder_1 (
    .in0(or_2_out), .in1(or_1_out), .in2(comparator_3_eq), .in3(1'b0), .out(priority_encoder_1_out),
    .en_out(priority_encoder_1_en_out));  // open: gs, en_in
  // Probe on multiplexer_4_out
  // Probe on Byte
  not not_2 (IMMen, comparator_1_eq);
  GPR gpr_1 (
    .Raddr1(Inst[18:15]), .Raddr2(Inst[23:20]), .CLK(CLK), .Wdata(multiplexer_4_out), .Waddr(Inst[10:7]),
    .Wen(not_1_out), .Rdata1(D1), .Rdata2(D2));
  or or_3 (MEMRen, comparator_4_eq, comparator_5_eq);
  or or_4 (MEMWen, comparator_6_eq, comparator_7_eq);
  or or_5 (Byte, comparator_5_eq, comparator_7_eq);
  // Probe on MEMRen
endmodule

module EX (
  input  [31:0] R1,
  input  [31:0] R2,
  input  [31:0] IMM,
  input  IMMen,
  output [31:0] EXout
);

  wire [31:0] multiplexer_1_out;

  Multiplexer #(.width(32)) multiplexer_1 (.in0(R2), .in1(IMM), .out(multiplexer_1_out), .sel(IMMen));
  Adder #(.width(32)) adder_1 (.a(R1), .b(multiplexer_1_out), .out(EXout));  // open: cin, cout
endmodule
